# Fritzing sketch schematic (saved by Fritzing 0.9.0b)
circuit board: 8.46667cm x 5.64444cm
breadboards: 1

parts:
  U1 = atmega328 [package=dip]
  IC1 = IC, DIP package, 14 pins [chip_label=4082]
  S1 = SWITCH-MOMENTARY-2 [package=tactile-pth]
  S2 = SWITCH-MOMENTARY-2 [package=tactile-pth]
  S3 = SWITCH-MOMENTARY-2 [package=tactile-pth]
  S4 = SWITCH-MOMENTARY-2 [package=tactile-pth]
  S5 = SWITCH-MOMENTARY-2 [package=tactile-pth]
  S6 = SWITCH-MOMENTARY-2 [package=tactile-pth]
  IRLED1 = LEDs [package=led10mm]
  R1 = Resistor [tolerance=±5% resistance=100 package=THT]
  XTAL1 = CRYSTAL - kHz [frequency="16 Mhz"]
  C1 = Capacitor [package=cap-pth-small2]
  C2 = Capacitor [package=cap-pth-small2]
  R2 = Resistor [tolerance=±5% resistance=10k package=THT]

nets (from the pcb view):
  N1: U1.RESET, R2.Pin_1
  N2: U1.D2, IC1.pin1
  N3: U1.D3_(PWM), R1.Pin_1
  N4: U1.VCC, U1.AVCC, U1.AREF, R2.Pin_0
  N5: U1.GND, IC1.pin7, S1.2, S2.2, S3.2, S4.2, S5.2, S6.2, IRLED1.C, C1.2, C2.2
  N6: U1.XLAT1, XTAL1.pin_0, C1.1
  N7: U1.XLAT2, XTAL1.pin_1, C2.1
  N8: U1.D7, IC1.pin5, S6.1
  N9: U1.D8, IC1.pin4, S5.1
  N10: U1.D9_(PWM), IC1.pin3, S4.1
  N11: U1.D10_(PWM), S3.1
  N12: U1.D11_(PWM), S2.1
  N13: U1.D12, S1.1
  N14: IRLED1.A, R1.Pin_0
